# Fritzing sketch Fritzing_B1WM (saved by Fritzing 0.9.2b)
breadboards: 1

parts:
  Part1 = Arduino Uno (Rev3)
  LED1 = LED - 5mm [color="White (4500K)" package="5 mm [THT]"]
  LED2 = LED - 5mm [color="White (4500K)" package="5 mm [THT]"]
  LED3 = LED - 5mm [color="White (4500K)" package="5 mm [THT]"]
  LED4 = LED - 5mm [color="White (4500K)" package="5 mm [THT]"]
  LED5 = LED - 5mm [color="White (4500K)" package="5 mm [THT]"]
  R1 = Resistor [tolerance=±5% resistance=220 package=THT]
  R2 = Resistor [tolerance=±5% resistance=220 package=THT]
  R3 = Resistor [tolerance=±5% resistance=220 package=THT]
  R4 = Resistor [tolerance=±5% resistance=220 package=THT]
  R5 = Resistor [tolerance=±5% resistance=220 package=THT]
  LED6 = RGB LED (com. cathode, rgb) [package="5 mm [THT]"]
  R6 = Photocell (LDR) [package=THT]
  R7 = Resistor [tolerance=±5% resistance=10k package=THT]
  R8 = Resistor [tolerance=±5% resistance=220 package=THT]
  R9 = Resistor [tolerance=±5% resistance=220 package=THT]
  R10 = Resistor [tolerance=±5% resistance=220 package=THT]

nets:
  N1: Part1.A0, R6.pin_1, R7.Pin_0
  N2: Part1.D9_PWM, R8.Pin_1
  N3: Part1.D10_PWM/SS, R9.Pin_1
  N4: Part1.D11_PWM/MOSI, R10.Pin_1
  N5: Part1.D3_PWM, R1.Pin_1
  N6: Part1.D4, R2.Pin_1
  N7: Part1.D5_PWM, R3.Pin_1
  N8: Part1.D6_PWM, R4.Pin_1
  N9: Part1.D7, R5.Pin_1
  N10: Part1.5V, R6.pin_0
  N11: Part1.GND, LED1.cathode, LED2.cathode, LED3.cathode, LED4.cathode, LED5.cathode, LED6.green_anode, R7.Pin_1
  N12: LED1.anode, R1.Pin_0
  N13: LED2.anode, R2.Pin_0
  N14: LED3.anode, R3.Pin_0
  N15: LED4.anode, R4.Pin_0
  N16: LED5.anode, R5.Pin_0
  N17: LED6.red_anode, R8.Pin_0
  N18: LED6.common_cathode, R9.Pin_0
  N19: LED6.blue_anode, R10.Pin_0
